// Logisim project 2-EXP.circ as structural Verilog: 1 circuit, main circuit main
module main (
  input  in_1,
  input  in_2,
  input  in_3,
  input  in_4,
  input  in_5,
  input  in_6,
  input  in_7,
  input  in_8,
  input  in_9,
  input  in_10,
  input  in_11,
  input  in_12,
  input  in_13,
  input  in_14,
  input  in_15,
  input  in_16,
  input  in_17,
  input  in_18,
  input  in_19,
  input  in_20,
  input  in_21,
  input  in_22,
  input  in_23,
  input  in_24,
  input  in_25,
  input  in_26,
  input  in_27,
  input  in_28,
  input  in_29,
  input  in_30,
  input  in_31,
  input  in_32
);

  wire clock_1_out, clock_2_out, clock_3_out, clock_4_out, clock_5_out, clock_6_out, clock_7_out,
       clock_8_out, d_ff_1_q, d_ff_2_q, d_ff_3_q, d_ff_4_q, d_ff_5_q, d_ff_6_q, d_ff_7_q, d_ff_8_q, d_ff_9_q,
       d_ff_10_q, d_ff_11_q, d_ff_12_q, d_ff_13_q, d_ff_14_q, d_ff_15_q, d_ff_16_q, d_ff_17_q, d_ff_18_q,
       d_ff_19_q, d_ff_20_q, d_ff_21_q, d_ff_22_q, d_ff_23_q, d_ff_24_q, d_ff_25_q, d_ff_26_q, d_ff_27_q,
       d_ff_28_q, d_ff_29_q, d_ff_30_q, d_ff_31_q, d_ff_32_q, undriven, undriven_2, undriven_3, undriven_4,
       undriven_5, undriven_6, undriven_7, undriven_8, undriven_9, undriven_10, undriven_11, undriven_12,
       undriven_13, undriven_14, undriven_15, undriven_16, undriven_17, undriven_18, undriven_19,
       undriven_20, undriven_21, undriven_22, undriven_23, undriven_24, undriven_25, undriven_26,
       undriven_27, undriven_28, undriven_29, undriven_30, undriven_31, undriven_32, xor_1_out, xor_2_out,
       xor_3_out, xor_4_out, xor_5_out, xor_6_out, xor_7_out, xor_8_out;

  Clock clock_1 (.out(clock_1_out));
  Clock clock_2 (.out(clock_2_out));
  Clock clock_3 (.out(clock_3_out));
  Clock clock_4 (.out(clock_4_out));
  LED led_1 (.in(d_ff_1_q));
  D_Flip_Flop d_ff_1 (.clk(clock_2_out), .D(d_ff_13_q), .Q(d_ff_1_q), .en(undriven_2));  // open: Qn, preset, reset
  LED led_2 (.in(d_ff_2_q));
  D_Flip_Flop d_ff_2 (.clk(clock_1_out), .D(d_ff_14_q), .Q(d_ff_2_q), .en(undriven));  // open: Qn, preset, reset
  xor xor_1 (xor_1_out, d_ff_1_q, d_ff_13_q);
  LED led_3 (.in(d_ff_3_q));
  D_Flip_Flop d_ff_3 (.clk(clock_3_out), .D(d_ff_15_q), .Q(d_ff_3_q), .en(undriven_3));  // open: Qn, preset, reset
  LED led_4 (.in(d_ff_4_q));
  D_Flip_Flop d_ff_4 (.clk(clock_4_out), .D(d_ff_16_q), .Q(d_ff_4_q), .en(undriven_4));  // open: Qn, preset, reset
  xor xor_2 (xor_2_out, d_ff_2_q, d_ff_14_q);
  LED led_5 (.in(d_ff_5_q));
  D_Flip_Flop d_ff_5 (.clk(clock_2_out), .D(xor_1_out), .Q(d_ff_5_q), .en(undriven_6));  // open: Qn, preset, reset
  xor xor_3 (xor_3_out, d_ff_3_q, d_ff_15_q);
  xor xor_4 (xor_4_out, d_ff_4_q, d_ff_16_q);
  LED led_6 (.in(d_ff_6_q));
  D_Flip_Flop d_ff_6 (.clk(clock_1_out), .D(xor_2_out), .Q(d_ff_6_q), .en(undriven_5));  // open: Qn, preset, reset
  LED led_7 (.in(d_ff_7_q));
  D_Flip_Flop d_ff_7 (.clk(clock_3_out), .D(xor_3_out), .Q(d_ff_7_q), .en(undriven_7));  // open: Qn, preset, reset
  LED led_8 (.in(d_ff_8_q));
  D_Flip_Flop d_ff_8 (.clk(clock_4_out), .D(xor_4_out), .Q(d_ff_8_q), .en(undriven_8));  // open: Qn, preset, reset
  LED led_9 (.in(d_ff_9_q));
  D_Flip_Flop d_ff_9 (.clk(clock_2_out), .D(d_ff_5_q), .Q(d_ff_9_q), .en(undriven_10));  // open: Qn, preset, reset
  LED led_10 (.in(d_ff_10_q));
  D_Flip_Flop d_ff_10 (.clk(clock_1_out), .D(d_ff_6_q), .Q(d_ff_10_q), .en(undriven_9));  // open: Qn, preset, reset
  LED led_11 (.in(d_ff_11_q));
  D_Flip_Flop d_ff_11 (.clk(clock_3_out), .D(d_ff_7_q), .Q(d_ff_11_q), .en(undriven_11));  // open: Qn, preset, reset
  LED led_12 (.in(d_ff_12_q));
  D_Flip_Flop d_ff_12 (.clk(clock_4_out), .D(d_ff_8_q), .Q(d_ff_12_q), .en(undriven_12));  // open: Qn, preset, reset
  D_Flip_Flop d_ff_13 (.clk(clock_2_out), .D(d_ff_9_q), .Q(d_ff_13_q), .en(undriven_14));  // open: Qn, preset, reset
  Clock clock_5 (.out(clock_5_out));
  LED led_13 (.in(d_ff_14_q));
  D_Flip_Flop d_ff_14 (.clk(clock_1_out), .D(d_ff_10_q), .Q(d_ff_14_q), .en(undriven_13));  // open: Qn, preset, reset
  LED led_14 (.in(d_ff_13_q));
  LED led_15 (.in(d_ff_15_q));
  D_Flip_Flop d_ff_15 (.clk(clock_3_out), .D(d_ff_11_q), .Q(d_ff_15_q), .en(undriven_15));  // open: Qn, preset, reset
  LED led_16 (.in(d_ff_16_q));
  D_Flip_Flop d_ff_16 (.clk(clock_4_out), .D(d_ff_12_q), .Q(d_ff_16_q), .en(undriven_16));  // open: Qn, preset, reset
  LED led_17 (.in(d_ff_17_q));
  D_Flip_Flop d_ff_17 (.clk(clock_5_out), .D(d_ff_23_q), .Q(d_ff_17_q), .en(undriven_17));  // open: Qn, preset, reset
  xor xor_5 (xor_5_out, d_ff_17_q, d_ff_23_q);
  LED led_18 (.in(d_ff_18_q));
  D_Flip_Flop d_ff_18 (.clk(clock_5_out), .D(xor_5_out), .Q(d_ff_18_q), .en(undriven_18));  // open: Qn, preset, reset
  Clock clock_6 (.out(clock_6_out));
  Clock clock_7 (.out(clock_7_out));
  Clock clock_8 (.out(clock_8_out));
  LED led_19 (.in(d_ff_19_q));
  D_Flip_Flop d_ff_19 (.clk(clock_5_out), .D(d_ff_18_q), .Q(d_ff_19_q), .en(undriven_19));  // open: Qn, preset, reset
  LED led_20 (.in(d_ff_20_q));
  D_Flip_Flop d_ff_20 (.clk(clock_6_out), .D(d_ff_30_q), .Q(d_ff_20_q), .en(undriven_20));  // open: Qn, preset, reset
  LED led_21 (.in(d_ff_21_q));
  D_Flip_Flop d_ff_21 (.clk(clock_7_out), .D(d_ff_31_q), .Q(d_ff_21_q), .en(undriven_21));  // open: Qn, preset, reset
  D_Flip_Flop d_ff_22 (.clk(clock_8_out), .D(d_ff_32_q), .Q(d_ff_22_q), .en(undriven_22));  // open: Qn, preset, reset
  xor xor_6 (xor_6_out, d_ff_20_q, d_ff_30_q);
  xor xor_7 (xor_7_out, d_ff_21_q, d_ff_31_q);
  LED led_22 (.in(d_ff_22_q));
  xor xor_8 (xor_8_out, d_ff_22_q, d_ff_32_q);
  LED led_23 (.in(d_ff_23_q));
  D_Flip_Flop d_ff_23 (.clk(clock_5_out), .D(d_ff_19_q), .Q(d_ff_23_q), .en(undriven_23));  // open: Qn, preset, reset
  LED led_24 (.in(d_ff_24_q));
  D_Flip_Flop d_ff_24 (.clk(clock_6_out), .D(xor_6_out), .Q(d_ff_24_q), .en(undriven_24));  // open: Qn, preset, reset
  LED led_25 (.in(d_ff_25_q));
  D_Flip_Flop d_ff_25 (.clk(clock_7_out), .D(xor_7_out), .Q(d_ff_25_q), .en(undriven_25));  // open: Qn, preset, reset
  D_Flip_Flop d_ff_26 (.clk(clock_8_out), .D(xor_8_out), .Q(d_ff_26_q), .en(undriven_26));  // open: Qn, preset, reset
  LED led_26 (.in(d_ff_26_q));
  LED led_27 (.in(d_ff_27_q));
  D_Flip_Flop d_ff_27 (.clk(clock_6_out), .D(d_ff_24_q), .Q(d_ff_27_q), .en(undriven_27));  // open: Qn, preset, reset
  LED led_28 (.in(d_ff_28_q));
  D_Flip_Flop d_ff_28 (.clk(clock_7_out), .D(d_ff_25_q), .Q(d_ff_28_q), .en(undriven_28));  // open: Qn, preset, reset
  D_Flip_Flop d_ff_29 (.clk(clock_8_out), .D(d_ff_26_q), .Q(d_ff_29_q), .en(undriven_29));  // open: Qn, preset, reset
  LED led_29 (.in(d_ff_29_q));
  LED led_30 (.in(d_ff_30_q));
  D_Flip_Flop d_ff_30 (.clk(clock_6_out), .D(d_ff_27_q), .Q(d_ff_30_q), .en(undriven_30));  // open: Qn, preset, reset
  LED led_31 (.in(d_ff_31_q));
  D_Flip_Flop d_ff_31 (.clk(clock_7_out), .D(d_ff_28_q), .Q(d_ff_31_q), .en(undriven_31));  // open: Qn, preset, reset
  D_Flip_Flop d_ff_32 (.clk(clock_8_out), .D(d_ff_29_q), .Q(d_ff_32_q), .en(undriven_32));  // open: Qn, preset, reset
  LED led_32 (.in(d_ff_32_q));

  // Notes on the sheet:
  //   1
  //   5
  //   3
  //   7
  //   0
  //   2
  //   4
  //   6
endmodule
