// Logisim project 6-EXP.circ as structural Verilog: 1 circuit, main circuit main
module main (
  input  in_1,
  input  [3:0] in_2,
  input  [3:0] in_3,
  input  [3:0] in_4,
  input  [3:0] in_5,
  input  in_6,
  input  [1:0] in_7,
  input  [3:0] in_8,
  input  [3:0] in_9,
  input  [3:0] in_10,
  input  [1:0] in_11,
  input  in_12,
  output out_13,
  output out_14
);

  wire and_1_out, nor_1_out, xnor_1_out, xor_1_out;
  wire [3:0] comparator_1_gt;
  wire [7:0] adder_1_out, multiplier_1_out, subtractor_1_out;
  wire [7:4] multiplier_1_cout, undriven, undriven_2;

  Adder adder_1 (.a({undriven_2, in_3}), .b({undriven, in_2}), .out(adder_1_out), .cin(in_1), .cout(out_13));
  Subtractor subtractor_1 (
    .a({undriven_2, in_3}), .b({undriven, in_2}), .out(subtractor_1_out), .bout(out_14));  // open: bin
  Multiplier multiplier_1 (
    .a({undriven_2, in_3}), .b({undriven, in_2}), .out(multiplier_1_out), .cout({multiplier_1_cout, in_5}));  // open: cin
  Comparator comparator_1 (
    .a({undriven_2, in_3}), .b({undriven, in_2}), .gt(comparator_1_gt[0]), .eq(comparator_1_gt[1]),
    .lt(comparator_1_gt[2]));
  Multiplexer #(.select(2)) multiplexer_1 (
    .in0(adder_1_out[0]), .in1(subtractor_1_out[0]), .in2(multiplier_1_out[0]), .in3(comparator_1_gt[0]),
    .out(in_4[0]), .sel(in_7), .en(in_6));
  and and_1 (and_1_out, in_8[0], in_9[0]);
  nor nor_1 (nor_1_out, in_8[0], in_9[0]);
  xor xor_1 (xor_1_out, in_8[0], in_9[0]);
  xnor xnor_1 (xnor_1_out, in_8[0], in_9[0]);
  Multiplexer #(.select(2)) multiplexer_2 (
    .in0(and_1_out), .in1(nor_1_out), .in2(xor_1_out), .in3(xnor_1_out), .out(in_10[0]), .sel(in_11),
    .en(in_12));
  // Pins of 1 and 4 bits meet at in_8
  // Pins of 1 and 4 bits meet at in_9
  // Pins of 4 and 8 bits meet at {undriven_2, in_3}
  // Pins of 4 and 8 bits meet at {undriven, in_2}
  // Pins of 1 and 8 bits meet at subtractor_1_out
  // Pins of 1 and 8 bits meet at adder_1_out
  // Pins of 1 and 8 bits meet at multiplier_1_out
  // Pins of 1 and 4 bits meet at comparator_1_gt
  // Pins of 1 and 4 bits meet at in_4
  // Pins of 4 and 8 bits meet at {multiplier_1_cout, in_5}
  // Pins of 1 and 4 bits meet at in_10
endmodule
