// Logisim project CSE.circ as structural Verilog: 1 circuit, main circuit main
module main (
  input  in_1,
  input  in_2,
  input  in_3,
  input  in_4,
  input  in_5,
  input  in_6,
  input  in_7,
  input  in_8,
  input  in_9,
  input  in_10,
  input  in_11,
  input  in_12
);

  Hex_Digit_Display hex_digit_display_1 (.value({in_1, in_2, in_3, in_4}));  // open: dp
  Hex_Digit_Display hex_digit_display_2 (.value({in_5, in_6, in_7, in_8}));  // open: dp
  Hex_Digit_Display hex_digit_display_3 (.value({in_9, in_10, in_11, in_12}));  // open: dp
endmodule
