// Logisim project EXPERIMENT3.circ as structural Verilog: 1 circuit, main circuit main
module main (
  input  INPUTS,
  input  in_2,
  input  D0,
  input  in_4,
  input  in_5,
  input  D1,
  input  D3,
  input  D4,
  input  in_9,
  input  in_10,
  input  in_11,
  input  in_12,
  input  in_13,
  input  [1:0] in_14
);

  wire AND_2_out, AND_3_out, AND_4_out, AND_out, controlled_inverter_1_out, controlled_inverter_2_out,
       multiplexer_1_out, OR_out;

  assign controlled_inverter_1_out = in_4 ? ~INPUTS : 1'bz;  // Controlled_Inverter controlled_inverter_1
  assign controlled_inverter_2_out = in_5 ? ~in_2 : 1'bz;  // Controlled_Inverter controlled_inverter_2
  and AND (AND_out, D0, controlled_inverter_1_out, controlled_inverter_2_out);
  and AND_2 (AND_2_out, D1, controlled_inverter_1_out, in_2);
  and AND_3 (AND_3_out, D3, INPUTS, controlled_inverter_2_out);
  and AND_4 (AND_4_out, D4, INPUTS, in_2);
  or OR (OR_out, AND_out, AND_2_out, AND_3_out, AND_4_out);
  Multiplexer #(.select(2)) multiplexer_1 (
    .in0(in_9), .in1(in_10), .in2(in_11), .in3(in_13), .out(multiplexer_1_out), .sel(in_14), .en(in_12));
  LED led_1 (.in(OR_out));
  LED led_2 (.in(multiplexer_1_out));

  // Notes on the sheet:
  //   S1
  //   S0
  //   DATA INPUTS
  //   DATA INPUTS
  //   4:1 MUX
  //   SELECT INPUTS
  //   OUTPUT
  //   LED
  //   OUTPUT
  //   ENABLE INPUT
  //   LED
endmodule
