// Logisim project EXperiment7part1 - Copy (2).circ as structural Verilog: 1 circuit, main circuit main
module main (
  input  [3:0] INPUT_B,
  input  [3:0] INPUT_A,
  input  CARRY___0,
  input  [3:0] ENABLE,
  input  [2:0] in_5,
  input  in_6,
  input  [3:0] in_7,
  output out_8,
  output out_9
);

  wire [3:0] adder_1_out, and_1_out, comparator_1_gt, multiplier_1_out, or_1_out, subtractor_1_out,
       xnor_1_out, xor_1_out;

  Adder #(.width(4)) adder_1 (.a(INPUT_A), .b(INPUT_B), .out(adder_1_out), .cin(CARRY___0), .cout(out_8));
  Subtractor #(.width(4)) subtractor_1 (.a(INPUT_A), .b(INPUT_B), .out(subtractor_1_out), .bout(out_9));  // open: bin
  Multiplier #(.width(4)) multiplier_1 (.a(INPUT_A), .b(INPUT_B), .out(multiplier_1_out), .cout(in_7));  // open: cin
  Comparator #(.width(4)) comparator_1 (
    .a(INPUT_A), .b(INPUT_B), .gt(comparator_1_gt[0]), .eq(comparator_1_gt[1]), .lt(comparator_1_gt[2]));
  assign and_1_out = INPUT_A & INPUT_B;  // AND_Gate and_1, 4 bits wide
  assign or_1_out = INPUT_A | INPUT_B;  // OR_Gate or_1, 4 bits wide
  assign xor_1_out = INPUT_A ^ INPUT_B;  // XOR_Gate xor_1, 4 bits wide
  assign xnor_1_out = ~(INPUT_A ^ INPUT_B);  // XNOR_Gate xnor_1, 4 bits wide
  Multiplexer #(.select(3), .width(4)) multiplexer_1 (
    .in0(adder_1_out), .in1(subtractor_1_out), .in2(multiplier_1_out), .in3(comparator_1_gt),
    .in4(and_1_out), .in5(or_1_out), .in6(xor_1_out), .in7(xnor_1_out), .out(ENABLE), .sel(in_5), .en(in_6));

  // Notes on the sheet:
  //   ARITHMETIC OPERATIONS
  //   OUTPUT C
  //   OUTPUT B
  //   CARRY OUT
  //   SPLITTER
  //   OUTPUT
endmodule
