// Logisim project EXperiment7part1 - Copy.circ as structural Verilog: 1 circuit, main circuit main
module main (
  input  [3:0] INPUT_B,
  input  [3:0] INPUT_A,
  input  CARRY___0,
  input  [3:0] ENABLE,
  input  [1:0] in_5,
  input  in_6,
  output out_7,
  output out_8
);

  wire [3:0] adder_1_out, subtractor_1_out, xnor_1_out, xor_1_out;

  Adder #(.width(4)) adder_1 (.a(INPUT_A), .b(INPUT_B), .out(adder_1_out), .cin(CARRY___0), .cout(out_7));
  Subtractor #(.width(4)) subtractor_1 (.a(INPUT_A), .b(INPUT_B), .out(subtractor_1_out), .bout(out_8));  // open: bin
  assign xor_1_out = INPUT_A ^ INPUT_B;  // XOR_Gate xor_1, 4 bits wide
  assign xnor_1_out = ~(INPUT_A ^ INPUT_B);  // XNOR_Gate xnor_1, 4 bits wide
  Multiplexer #(.select(2), .width(4)) multiplexer_1 (
    .in0(adder_1_out), .in1(subtractor_1_out), .in2(xor_1_out), .in3(xnor_1_out), .out(ENABLE), .sel(in_5),
    .en(in_6));

  // Notes on the sheet:
  //   ARITHMETIC OPERATIONS
  //   OUTPUT C
  //   OUTPUT B
  //   OUTPUT
  //   SELECT INPUT
endmodule
