// Logisim project EXperiment7part2.circ as structural Verilog: 1 circuit, main circuit main
module main (
  input  [3:0] INPUT_B,
  input  [3:0] INPUT_A,
  input  [3:0] OUTPUT,
  input  in_4,
  input  [1:0] in_5
);

  wire [3:0] AND_out, NOR_out, XNOR_out, XOR_out;

  assign AND_out = INPUT_B & INPUT_A;  // AND_Gate AND, 4 bits wide
  assign NOR_out = ~(INPUT_B | INPUT_A);  // NOR_Gate NOR, 4 bits wide
  assign XOR_out = INPUT_B ^ INPUT_A;  // XOR_Gate XOR, 4 bits wide
  assign XNOR_out = ~(INPUT_B ^ INPUT_A);  // XNOR_Gate XNOR, 4 bits wide
  Multiplexer #(.select(2), .width(4)) multiplexer_1 (
    .in0(AND_out), .in1(NOR_out), .in2(XOR_out), .in3(XNOR_out), .out(OUTPUT), .sel(in_5), .en(in_4));

  // Notes on the sheet:
  //   LOGICAL OPERATIONS
  //   ENABLE INPUT
  //   SELECT INPUT
endmodule
