// Logisim project Experiment 8.circ as structural Verilog: 1 circuit, main circuit main
module main (
  input  [3:0] in_1,
  input  [3:0] in_2,
  input  [3:0] in_3,
  input  [1:0] in_4,
  input  [1:0] in_5,
  input  [3:0] in_6,
  output [3:0] out_7,
  output [3:0] out_8,
  output [3:0] out_9,
  output [3:0] out_10,
  output [3:0] out_11,
  output [3:0] out_12,
  output [3:0] out_13,
  output [3:0] out_14
);

  wire clock_1_out;
  wire [3:0] demultiplexer_1_out0, demultiplexer_1_out1, demultiplexer_1_out2, demultiplexer_1_out3,
       multiplexer_1_out;

  Clock clock_1 (.out(clock_1_out));
  Register #(.width(4)) register_1 (.D(in_1), .Q(out_8), .clk(clock_1_out));  // open: en, clr
  Register #(.width(4)) register_2 (.D(in_2), .Q(out_10), .clk(clock_1_out));  // open: en, clr
  Register #(.width(4)) register_3 (.D(in_3), .Q(out_11), .clk(clock_1_out));  // open: en, clr
  Register #(.width(4)) register_4 (.D(in_6), .Q(out_14), .clk(clock_1_out));  // open: en, clr
  Multiplexer #(.select(2), .width(4), .enable("false")) multiplexer_1 (
    .in0(out_8), .in1(out_10), .in2(out_11), .in3(out_14), .out(multiplexer_1_out), .sel(in_4));
  Demultiplexer #(.select(2), .width(4), .enable("false")) demultiplexer_1 (
    .out0(demultiplexer_1_out0), .out1(demultiplexer_1_out1), .out2(demultiplexer_1_out2),
    .out3(demultiplexer_1_out3), .in(multiplexer_1_out), .sel(in_5));
  Register #(.width(4)) register_5 (.D(demultiplexer_1_out0), .Q(out_7), .clk(clock_1_out));  // open: en, clr
  Register #(.width(4)) register_6 (.D(demultiplexer_1_out1), .Q(out_9), .clk(clock_1_out));  // open: en, clr
  Register #(.width(4)) register_7 (.D(demultiplexer_1_out2), .Q(out_12), .clk(clock_1_out));  // open: en, clr
  Register #(.width(4)) register_8 (.D(demultiplexer_1_out3), .Q(out_13), .clk(clock_1_out));  // open: en, clr
endmodule
