// Logisim project PRoject2.circ as structural Verilog: 1 circuit, main circuit main
module main (
  input  Key,
  input  Car_Door,
  input  Seatbelt
);

  wire AND3_out, AND_2_out, AND_out, controlled_inverter_1_out, controlled_inverter_2_out, OR_out;

  Controlled_Inverter controlled_inverter_1 (.in(Car_Door), .out(controlled_inverter_1_out));  // open: en
  Controlled_Inverter controlled_inverter_2 (.in(Seatbelt), .out(controlled_inverter_2_out));  // open: en
  and AND (AND_out, Key, controlled_inverter_1_out);
  and AND3 (AND3_out, Key, controlled_inverter_2_out);
  and AND_2 (AND_2_out, Key, Car_Door, Seatbelt);
  LED led_1 (.in(AND_2_out));
  or OR (OR_out, AND_out, AND3_out);
  LED led_2 (.in(OR_out));

  // Notes on the sheet:
  //   Engine
  //   BUZZER
endmodule
